# Fritzing sketch EnerginoBis (saved by Fritzing 0.7.9b)
breadboards: 1

parts:
  100k = Resistor [tolerance=±5% resistance=100k package=THT]
  +_IN_- = Screw terminal - 2 pins [package=THT]
  10k = Resistor [tolerance=±5% resistance=10k package=THT]
  +_OUT_- = Screw terminal - 2 pins [package=THT]
  Q1 = NPN-Transistor [package="TO92 [THT]"]
  1k = Resistor [tolerance=±5% resistance=1k package=THT]
  10k_2 = Resistor [tolerance=±5% resistance=10k package=THT]
  D1 = Rectifier Diode [part_number=1N4001 package="300 mil [THT]"]
  IC1 = IC, DIP package, 12 pins [chip_label=Relay spacing=300mil]
  Part2 = SO08 [chip_label=SOIC-14 spacing=300mil package=SO]
  0_1uF = Ceramic Capacitor [capacitance=0.1µF package="100 mil [THT, multilayer]"]
  1nF = Ceramic Capacitor [capacitance=1nF package="100 mil [THT, multilayer]"]
  1k_2 = Resistor [tolerance=±5% resistance=220 package=THT]
  Energino_v2 = Arduino
  47k = Resistor [tolerance=±5% resistance=220 package=THT]
  47k_2 = Resistor [tolerance=±5% resistance=220 package=THT]
  OPA344 = IC, DIP package, 8 pins [chip_label=IC]
  47k_3 = Resistor [tolerance=±5% resistance=220 package=THT]
  0_1uF_2 = Ceramic Capacitor [capacitance=0.1µF package="100 mil [THT, multilayer]"]
  0_1uF_3 = Ceramic Capacitor [capacitance=0.1µF package="100 mil [THT, multilayer]"]
  0_1uF_4 = Ceramic Capacitor [capacitance=0.1µF package="100 mil [THT, multilayer]"]

nets:
  N1: 100k.Pin_0, 10k.Pin_1, Energino_v2.A1
  N2: 100k.Pin_1, +_IN_-.pin1, Part2.1, Part2.2
  N3: +_IN_-.pin2, 10k.Pin_0, +_OUT_-.pin2, Q1.E, 10k_2.Pin_0, Part2.5, 0_1uF.1, 1nF.1, Energino_v2.GND, 47k_2.Pin_0, OPA344.pin4, 0_1uF_2.1, 0_1uF_3.1
  N4: +_OUT_-.pin1, IC1.pin4
  N5: Q1.B, 1k.Pin_0, 10k_2.Pin_1
  N6: Q1.C, D1.anode, IC1.pin12
  N7: 1k.Pin_1, Energino_v2.D2
  N8: D1.cathode, IC1.pin7, Part2.8, 0_1uF.0, Energino_v2.+5V, 47k.Pin_0, OPA344.pin7, 0_1uF_3.0
  N9: IC1.pin1, Part2.3, Part2.4
  N10: Part2.6, 1nF.0
  N11: Part2.7, 1k_2.Pin_1
  N12: 1k_2.Pin_0, OPA344.pin2, 47k_3.Pin_1, 0_1uF_4.1
  N13: Energino_v2.A0, OPA344.pin6, 47k_3.Pin_0, 0_1uF_4.0
  N14: 47k.Pin_1, 47k_2.Pin_1, OPA344.pin3, 0_1uF_2.0
